// Logisim project lab.circ as structural Verilog: 1 circuit, main circuit main
module main (
);

  wire clock_1_out, incrementer_1_p1, registerfile_1_p1, registerfile_1_p7;
  wire [4:0] multiplexer_2_out;
  wire [31:0] incrementer_1_p4, mipsprogramrom_1_p1, multiplexer_1_out, register_1_q, registerfile_1_p8,
       shifter_1_out, shifter_2_out;

  Clock clock_1 (.out(clock_1_out));
  Register #(.width(32)) register_1 (
    .D(shifter_2_out), .en(1'b1), .clk(clock_1_out), .Q(register_1_q), .clr(incrementer_1_p1));
  Shifter #(.width(32), .shift("lr")) shifter_1 (.in(register_1_q), .\dist (5'b00010), .out(shifter_1_out));
  // Incrementer #(.width(32)) incrementer_1: pin names not known; wires that end beside it: incrementer_1_p1, register_1_q, shifter_1_out, incrementer_1_p4
  // MIPSProgramROM mipsprogramrom_1: pin names not known; wires that end beside it: mipsprogramrom_1_p1, mipsprogramrom_1_p1, mipsprogramrom_1_p1[5:0], mipsprogramrom_1_p1[10:6]
  Shifter #(.width(32)) shifter_2 (.in(incrementer_1_p4), .\dist (5'b00010), .out(shifter_2_out));
  Shifter #(.width(26)) shifter_3 (.in(mipsprogramrom_1_p1[25:0]), .\dist (5'b00010));  // open: out
  Multiplexer #(.width(32), .enable("false")) multiplexer_1 (
    .in0(registerfile_1_p8), .in1({{16{1'b0}}, mipsprogramrom_1_p1[15:0]}), .out(multiplexer_1_out),
    .sel(mipsprogramrom_1_p1[29]));
  Multiplexer #(.width(5), .enable("false")) multiplexer_2 (
    .in0(mipsprogramrom_1_p1[15:11]), .in1(mipsprogramrom_1_p1[20:16]), .out(multiplexer_2_out),
    .sel(mipsprogramrom_1_p1[29]));
  // RegisterFile registerfile_1: pin names not known; wires that end beside it: registerfile_1_p1, clock_1_out, 1'b1, multiplexer_2_out, mipsprogramrom_1_p1[25:21], mipsprogramrom_1_p1[20:16], registerfile_1_p7, registerfile_1_p8
  // Mips_ALU mips_alu_1: pin names not known; wires that end beside it: registerfile_1_p7, multiplexer_1_out, 4'b0010, registerfile_1_p1

  // Notes on the sheet:
  //   contents of mipsprogramrom_1 (hex, n*v repeats v):
  //   addiu $s1, $zero, 2 addu $s2, $s0, $s1
  //   target add
  //   imm
  //   op
  //   rs
  //   rt
  //   rd
  //   shamt
  //   funct
endmodule
