// Logisim project lab2.circ as structural Verilog: 4 circuits, main circuit main
module main (
);

  wire ALUSrc, and_1_out, Branch, Clk, Jump, MemtoReg, mips_alu_1_p3, RegDst, registerfile_1_p6, Zero;
  wire [4:0] multiplexer_1_out;
  wire [5:0] Func, Op;
  wire [15:6] Imm;
  wire [25:16] Instruction;
  wire [27:0] PcPlus4;
  wire [31:0] adder_1_out, mips_alu_1_p5, mips_ram_1_p2, multiplexer_2_out, multiplexer_3_out, NextPC, PC,
       registerfile_1_p1, shifter_2_out, SignExt, WriteData;
  wire [31:2] JumpAddress;

  Clock clock_1 (.out(Clk));
  Register #(.width(32)) register_1 (.D(NextPC), .en(1'b1), .clk(Clk), .Q(PC));  // open: clr
  Shifter #(.width(26)) shifter_1 (.in({Instruction, Imm, Func}), .\dist (5'b00010), .out(JumpAddress[27:2]));
  SignExtend signextend_1 (.in_1({Imm, Func}), .out_2(SignExt));
  plus4 plus4_1 (.in_1(PC), .out_2({JumpAddress[31:28], PcPlus4}));
  // MIPSProgramROM mipsprogramrom_1: pin names not known; wires that end beside it: PC, {Op, Instruction, Imm, Func}
  Shifter #(.width(32)) shifter_2 (.in(SignExt), .\dist (5'b00010), .out(shifter_2_out));
  Multiplexer #(.width(5), .enable("false")) multiplexer_1 (
    .in0(Instruction[20:16]), .in1(Imm[15:11]), .out(multiplexer_1_out), .sel(RegDst));
  Adder #(.width(32)) adder_1 (
    .a({JumpAddress[31:28], PcPlus4}), .b(shifter_2_out), .out(adder_1_out));  // open: cin, cout
  // RegisterFile registerfile_1: pin names not known; wires that end beside it: registerfile_1_p1, Clk, multiplexer_1_out, Instruction[25:21], Instruction[20:16], registerfile_1_p6, WriteData
  Multiplexer #(.width(32), .enable("false")) multiplexer_2 (
    .in0({JumpAddress[31:28], PcPlus4}), .in1(adder_1_out), .out(multiplexer_2_out), .sel(and_1_out));
  and and_1 (and_1_out, Branch, Zero);
  Multiplexer #(.width(32), .enable("false")) multiplexer_3 (
    .in0(WriteData), .in1(SignExt), .out(multiplexer_3_out), .sel(ALUSrc));
  // Mips_ALU mips_alu_1: pin names not known; wires that end beside it: registerfile_1_p6, multiplexer_3_out, mips_alu_1_p3, mips_alu_1_p3, mips_alu_1_p5, mips_alu_1_p5[23:0], WriteData
  Multiplexer #(.width(32), .enable("false")) multiplexer_4 (
    .in0(multiplexer_2_out), .in1({JumpAddress, 2'b00}), .out(NextPC), .sel(Jump));
  // MIPS_RAM #(.addrWidth(24)) mips_ram_1: pin names not known; wires that end beside it: Clk, mips_ram_1_p2
  Multiplexer #(.width(32), .enable("false")) multiplexer_5 (
    .in0(mips_alu_1_p5), .in1(mips_ram_1_p2), .out(registerfile_1_p1), .sel(MemtoReg));

  // Other names for the same wires on the sheet: Imm[5:0] = Func; Instruction[15:0] = {Imm, Func};
  //   Shamt[4:0] = Imm[10:6]; Rd[4:0] = Imm[15:11]; Rt[4:0] = Instruction[20:16]; Rs[4:0] = Instruction[25:21];
  //   PcPlus4[31:28] = JumpAddress[31:28]

  // Notes on the sheet:
  //   contents of mipsprogramrom_1 (hex, n*v repeats v):
  //   addiu $s1, $zero, 2 addu $s2, $s0, $s1
endmodule

module plus4 (
  input  [31:0] in_1,
  output [31:0] out_2
);

  wire [31:0] incrementer_1_p2, shifter_1_out;

  Shifter #(.width(32), .shift("lr")) shifter_1 (.in(in_1), .\dist (5'b00010), .out(shifter_1_out));
  // Incrementer #(.width(32)) incrementer_1: pin names not known; wires that end beside it: shifter_1_out, incrementer_1_p2
  Shifter #(.width(32)) shifter_2 (.in(incrementer_1_p2), .\dist (5'b00010), .out(out_2));
endmodule

module SignExtend (
  input  [15:0] in_1,
  output [31:0] out_2
);


  assign out_2 = {{17{in_1[15]}}, in_1[14:0]};
endmodule

module Add (
  input  [31:0] in_1,
  input  [31:0] in_2,
  output [31:0] out_3,
  output out_4
);

  Adder #(.width(32)) adder_1 (.a(in_1), .b(in_2), .out(out_3), .cout(out_4));  // open: cin
endmodule
