// Logisim project mips_single.circ as structural Verilog: 16 circuits, main circuit main
module main (
  input  [3:0] in_1,
  output [31:0] out_2
);

  wire alu_1_zero, and_1_out, Clk, sel_1_alusrc, sel_1_branch, sel_1_jump, sel_1_memread, sel_1_memtoreg,
       sel_1_memwrite, sel_1_regdst, sel_1_regwrite;
  wire [3:0] alucontrol_1_out_3;
  wire [4:0] instruction_1_rd_15_11, instruction_1_rs_25_21, instruction_1_rt_20_16,
       instruction_1_shamt_10_6, multiplexer_1_out;
  wire [5:0] instruction_1_func_5_0, instruction_1_op_31_26;
  wire [15:0] instruction_1_imm16_15_0;
  wire [25:0] instruction_1_imm26;
  wire [27:0] shiftleft2_1_out_2;
  wire [31:0] adder_1_out, datamemory_1_data_out, extender_1_extened, mipsprogramrom_1_p2, multiplexer_2_out,
       multiplexer_3_out, multiplexer_4_out, multiplexer_5_out, plus4_1_pc_plus_4, register_1_q,
       registers_1_busa, registers_1_busb, shifter_1_out;

  Register #(.width(32)) register_1 (.D(multiplexer_4_out), .en(1'b1), .clk(Clk), .Q(register_1_q));  // open: clr
  Plus4 plus4_1 (.Pc(register_1_q), .Pc_plus_4(plus4_1_pc_plus_4));
  Clock clock_1 (.out(Clk));
  // MIPSProgramROM mipsprogramrom_1: pin names not known; wires that end beside it: register_1_q, mipsprogramrom_1_p2, mipsprogramrom_1_p2
  Sel sel_1 (
    .Func(instruction_1_func_5_0), .Op(instruction_1_op_31_26), .RegDst(sel_1_regdst), .Jump(sel_1_jump),
    .Branch(sel_1_branch), .MemRead(sel_1_memread), .MemtoReg(sel_1_memtoreg), .MemWrite(sel_1_memwrite),
    .ALUSrc(sel_1_alusrc), .RegWrite(sel_1_regwrite));
  Instruction instruction_1 (
    .in_1(mipsprogramrom_1_p2), .Imm26(instruction_1_imm26), .Op_31_26(instruction_1_op_31_26),
    .Rs_25_21(instruction_1_rs_25_21), .Rt_20_16(instruction_1_rt_20_16), .Rd_15_11(instruction_1_rd_15_11),
    .Imm16_15_0(instruction_1_imm16_15_0), .Shamt_10_6(instruction_1_shamt_10_6),
    .Func_5_0(instruction_1_func_5_0));
  Multiplexer #(.width(5), .enable("false")) multiplexer_1 (
    .in0(instruction_1_rt_20_16), .in1(instruction_1_rd_15_11), .out(multiplexer_1_out), .sel(sel_1_regdst));
  Shiftleft2 shiftleft2_1 (.Imm26(instruction_1_imm26), .out_2(shiftleft2_1_out_2));
  ALUControl alucontrol_1 (.ALUOp(instruction_1_op_31_26), .Func(instruction_1_func_5_0), .out_3(alucontrol_1_out_3));
  Registers registers_1 (
    .RegWrite(sel_1_regwrite), .RA(instruction_1_rs_25_21), .RB(instruction_1_rt_20_16),
    .RW(multiplexer_1_out), .Clk(Clk), .BusW(multiplexer_5_out), .BusA(registers_1_busa),
    .BusB(registers_1_busb));
  Extender extender_1 (.Imm16(instruction_1_imm16_15_0), .Extened(extender_1_extened));
  Shifter #(.width(32)) shifter_1 (.in(extender_1_extened), .\dist (5'b00010), .out(shifter_1_out));
  Multiplexer #(.width(32), .enable("false")) multiplexer_2 (
    .in0(registers_1_busb), .in1(extender_1_extened), .out(multiplexer_2_out), .sel(sel_1_alusrc));
  Adder #(.width(32)) adder_1 (.a(plus4_1_pc_plus_4), .b(shifter_1_out), .out(adder_1_out));  // open: cin, cout
  and and_1 (and_1_out, sel_1_branch, alu_1_zero);
  ALU alu_1 (
    .A(registers_1_busa), .B(multiplexer_2_out), .Op(alucontrol_1_out_3), .Sa(instruction_1_shamt_10_6),
    .Zero(alu_1_zero), .ALUOut(out_2));
  Multiplexer #(.width(32), .enable("false")) multiplexer_3 (
    .in0(plus4_1_pc_plus_4), .in1(adder_1_out), .out(multiplexer_3_out), .sel(and_1_out));
  Multiplexer #(.width(32), .enable("false")) multiplexer_4 (
    .in0(multiplexer_3_out), .in1({plus4_1_pc_plus_4[31:28], shiftleft2_1_out_2}), .out(multiplexer_4_out),
    .sel(sel_1_jump));
  Multiplexer #(.width(32), .enable("false")) multiplexer_5 (
    .in0(out_2), .in1(datamemory_1_data_out), .out(multiplexer_5_out), .sel(sel_1_memtoreg));
  DataMemory datamemory_1 (
    .Address(out_2), .Data_in(registers_1_busb), .Store(sel_1_memwrite), .SelectBytes(in_1), .Clk(Clk),
    .Load(sel_1_memread), .Data_out(datamemory_1_data_out));

  // Notes on the sheet:
  //   contents of mipsprogramrom_1 (hex, n*v repeats v):
  //   addiu $29, $29, -4      addiu $8, $0, 7         sw $8, 0($29)   jal r_hailstone         addiu $29,
  //   $29, 4       j exit  r_hailstone:    lw $9, 0($29)           # load n        addiu $10, $0, 1
  //   bne $9, $10, r_hailstone_recur_elseif   lui $2, 0       jr $31   r_hailstone_recur_elseif:      lw
  //   $9, 0($29)           # load n        andi $10, $9, 1 # check n % 2   bne $10, $0,
  //   r_hailstone_recur_else             addiu $29, $29, -8      sw $31, 4($29)  sw $30, 0($29)  addu $30,
  //   $0, $29       lw $10, 8($30)          # load n                # n % 2 == 0    sra $10, $10, 1
  //   # n / 2                 addiu $29, $29, -4      sw $10, 0($29)  # call r_hailstone(n/2);        jal
  //   r_hailstone         addiu $29, $29, 4               # 1 + r_hailstone(n/2);         addiu $2, $2, 1
  //   lw $31, 4($30)  lw $30, 0($30)  addiu $29, $29, 8       jr $31   r_hailstone_recur_else:
  //   addiu $29, $29, -8      sw $31, 4($29)  sw $30, 0($29)  addu $30, $0, $29       lw $10, 8($30)
  //   # load n        # n * 3         addu $11, $0, $10       addu $11, $11, $10      addu $11, $11, $10
  //   addiu $11, $11, 0x1     # n + 1                 addiu $29, $29, -4      sw $11, 0($29)  # call
  //   r_hailstone(3*n+1);      jal r_hailstone         addiu $29, $29, 4               # 1 +
  //   r_hailstone(3*n+1);       addiu $2, $2, 1                 lw $31, 4($30)  lw $30, 0($30)  addiu $29,
  //   $29, 8       jr $31   exit:
endmodule

module Plus4 (
  input  [31:0] Pc,
  output [31:0] Pc_plus_4
);

  // Incrementer #(.width(30)) incrementer_1: pin names not known; wires that end beside it: Pc[31:2], Pc_plus_4[31:2]

  assign Pc_plus_4[1:0] = Pc[1:0];
endmodule

module Instruction (
  input  [31:0] in_1,
  output [25:0] Imm26,
  output [5:0] Op_31_26,
  output [4:0] Rs_25_21,
  output [4:0] Rt_20_16,
  output [4:0] Rd_15_11,
  output [15:0] Imm16_15_0,
  output [4:0] Shamt_10_6,
  output [5:0] Func_5_0
);


  assign Func_5_0 = in_1[5:0];
  assign Imm16_15_0 = in_1[15:0];
  assign Imm26 = in_1[25:0];
  assign Op_31_26 = in_1[31:26];
  assign Rd_15_11 = in_1[15:11];
  assign Rs_25_21 = in_1[25:21];
  assign Rt_20_16 = in_1[20:16];
  assign Shamt_10_6 = in_1[10:6];
endmodule

module Extender (
  input  [15:0] Imm16,
  output [31:0] Extened
);

  and and_1 (Extened[31], 1'b1, Imm16[15]);

  assign Extened[30:0] = {{15{Extened[31]}}, Imm16};
endmodule

module Registers (
  input  RegWrite,
  input  [4:0] RA,
  input  [4:0] RB,
  input  [4:0] RW,
  input  Clk,
  input  [31:0] BusW,
  output [31:0] BusA,
  output [31:0] BusB
);

  // RegisterFile registerfile_1: pin names not known; wires that end beside it: BusW, Clk, RegWrite, RW, RA, RB, BusA, BusB
endmodule

module ALU (
  input  [31:0] A,
  input  [31:0] B,
  input  [3:0] Op,
  input  [4:0] Sa,
  output Zero,
  output [31:0] ALUOut
);

  wire [31:0] not_1_out;

  // Mips_ALU mips_alu_1: pin names not known; wires that end beside it: A, B, Op, Sa, ALUOut
  assign not_1_out = ~ALUOut;  // NOT_Gate not_1, 32 bits wide
  and and_1 (Zero, not_1_out[0], not_1_out[1], not_1_out[2], not_1_out[3], not_1_out[4], not_1_out[5], not_1_out[6], not_1_out[7], not_1_out[8], not_1_out[9], not_1_out[10], not_1_out[11], not_1_out[12], not_1_out[13], not_1_out[14], not_1_out[15], not_1_out[16], not_1_out[17], not_1_out[18], not_1_out[19], not_1_out[20], not_1_out[21], not_1_out[22], not_1_out[23], not_1_out[24], not_1_out[25], not_1_out[26], not_1_out[27], not_1_out[28], not_1_out[29], not_1_out[30], not_1_out[31]);
endmodule

module DataMemory (
  input  [31:0] Address,
  input  [31:0] Data_in,
  input  Store,
  input  [3:0] SelectBytes,
  input  Clk,
  input  Load,
  output [31:0] Data_out
);

  // MIPS_RAM #(.addrWidth(24)) mips_ram_1: pin names not known; wires that end beside it: Address[23:0], Data_in, Store, SelectBytes, Clk, Load, Data_out
endmodule

module Shiftleft2 (
  input  [25:0] Imm26,
  output [27:0] out_2
);

  Shifter #(.width(26)) shifter_1 (.in(Imm26), .\dist (5'b00010), .out(out_2[27:2]));

  assign out_2[1:0] = 2'b00;
endmodule

module Control (
  input  [5:0] Op,
  output RegDst,
  output Jump,
  output Branch,
  output MemRead,
  output MemtoReg,
  output [3:0] ALUOp,
  output MemWrite,
  output ALUSrc,
  output RegWrite
);


  assign ALUOp = Op[3:0];
  assign ALUSrc = Op[1];
  assign Branch = Op[3];
  assign Jump = Op[2];
  assign MemRead = Op[4];
  assign MemtoReg = Op[5];
  assign MemWrite = Op[0];
  assign RegDst = Op[1];
  assign RegWrite = Op[2];
endmodule

module ALUControl (
  input  [5:0] ALUOp,
  input  [5:0] Func,
  output [3:0] out_3
);

  wire allzero_1_allzero, functoalu_1_alu1, functoalu_1_alu2, functoalu_1_alu3, functoalu_1_alu4,
       optoalu_1_alu1, optoalu_1_alu2, optoalu_1_alu3, optoalu_1_alu4;

  AllZero allzero_1 (.Inp(ALUOp), .AllZero(allzero_1_allzero));
  FuncToAlu functoalu_1 (
    .F1(Func[5]), .F2(Func[4]), .F3(Func[3]), .F4(Func[2]), .F5(Func[1]), .F6(Func[0]),
    .Alu1(functoalu_1_alu1), .Alu2(functoalu_1_alu2), .Alu3(functoalu_1_alu3), .Alu4(functoalu_1_alu4));
  OpToAlu optoalu_1 (
    .Op1(ALUOp[5]), .Op2(ALUOp[4]), .Op3(ALUOp[3]), .Op4(ALUOp[2]), .Op5(ALUOp[1]), .Op6(ALUOp[0]),
    .Alu1(optoalu_1_alu1), .Alu2(optoalu_1_alu2), .Alu3(optoalu_1_alu3), .Alu4(optoalu_1_alu4));
  Multiplexer #(.enable("false")) multiplexer_1 (
    .in0(functoalu_1_alu1), .in1(optoalu_1_alu1), .out(out_3[3]), .sel(allzero_1_allzero));
  Multiplexer #(.enable("false")) multiplexer_2 (
    .in0(functoalu_1_alu2), .in1(optoalu_1_alu2), .out(out_3[2]), .sel(allzero_1_allzero));
  Multiplexer #(.enable("false")) multiplexer_3 (
    .in0(functoalu_1_alu3), .in1(optoalu_1_alu3), .out(out_3[1]), .sel(allzero_1_allzero));
  Multiplexer #(.enable("false")) multiplexer_4 (
    .in0(functoalu_1_alu4), .in1(optoalu_1_alu4), .out(out_3[0]), .sel(allzero_1_allzero));
endmodule

module Comm1 (
  input  [5:0] Op,
  output RegDst,
  output Jump,
  output Branch,
  output MemRead,
  output MemtoReg,
  output MemWrite,
  output ALUSrc,
  output RegWrite
);

  wire and_2_out, and_3_out, and_4_out, and_5_out, and_6_out, and_7_out, and_8_out, and_9_out, and_10_out,
       and_11_out, and_12_out, and_13_out, and_14_out, not_1_out, not_2_out, not_3_out, not_4_out, not_5_out,
       not_6_out, not_7_out, not_8_out, not_9_out, not_10_out, not_11_out, not_12_out, not_13_out,
       not_14_out, not_15_out;

  not not_1 (not_1_out, Op[5]);
  not not_2 (not_2_out, Op[3]);
  not not_3 (not_3_out, Op[2]);
  not not_4 (not_4_out, Op[3]);
  not not_5 (not_5_out, Op[2]);
  not not_6 (not_6_out, Op[0]);
  not not_7 (not_7_out, Op[5]);
  not not_8 (not_8_out, Op[3]);
  not not_9 (not_9_out, Op[1]);
  not not_10 (not_10_out, Op[5]);
  not not_11 (not_11_out, Op[3]);
  not not_12 (not_12_out, Op[3]);
  not not_13 (not_13_out, Op[3]);
  and and_1 (MemWrite, Op[5], Op[3]);
  and and_2 (and_2_out, Op[5], Op[1]);
  and and_3 (and_3_out, Op[5], Op[2]);
  not not_14 (not_14_out, Op[5]);
  not not_15 (not_15_out, Op[3]);
  and and_4 (and_4_out, not_1_out, not_2_out, not_3_out);
  or or_1 (Jump, and_4_out, and_5_out);
  and and_5 (and_5_out, not_4_out, not_5_out, not_6_out);
  and and_6 (and_6_out, not_7_out, not_8_out, not_9_out);
  or or_2 (Branch, and_6_out, and_7_out);
  and and_7 (and_7_out, not_10_out, not_11_out, Op[0]);
  and and_8 (and_8_out, Op[5], not_12_out, Op[1]);
  or or_3 (MemRead, and_8_out, and_9_out);
  and and_9 (and_9_out, Op[5], Op[2]);
  and and_10 (and_10_out, not_13_out, Op[2]);
  or or_4 (MemtoReg, and_10_out, and_11_out);
  and and_11 (and_11_out, Op[5], Op[1]);
  or or_5 (ALUSrc, Op[3], and_2_out, and_3_out);
  and and_12 (and_12_out, not_14_out, Op[3]);
  and and_13 (and_13_out, Op[5], not_15_out, Op[1]);
  or or_6 (RegWrite, and_12_out, and_13_out, and_14_out);
  and and_14 (and_14_out, Op[5], Op[2]);

  assign RegDst = 1'b0;
endmodule

module AllZero (
  input  [5:0] Inp,
  output AllZero
);

  or or_1 (AllZero, Inp[0], Inp[1], Inp[2], Inp[3], Inp[4], Inp[5]);
endmodule

module Sel (
  input  [5:0] Func,
  input  [5:0] Op,
  output RegDst,
  output Jump,
  output Branch,
  output MemRead,
  output MemtoReg,
  output MemWrite,
  output ALUSrc,
  output RegWrite
);

  wire allzero_1_allzero, comm1_1_alusrc, comm1_1_branch, comm1_1_jump, comm1_1_memread, comm1_1_memtoreg,
       comm1_1_memwrite, comm1_1_regdst, comm1_1_regwrite, comm2_1_alusrc, comm2_1_branch, comm2_1_jump,
       comm2_1_memread, comm2_1_memtoreg, comm2_1_memwrite, comm2_1_regdst, comm2_1_regwrite;

  Comm1 comm1_1 (
    .Op(Op), .RegDst(comm1_1_regdst), .Jump(comm1_1_jump), .Branch(comm1_1_branch),
    .MemRead(comm1_1_memread), .MemtoReg(comm1_1_memtoreg), .MemWrite(comm1_1_memwrite),
    .ALUSrc(comm1_1_alusrc), .RegWrite(comm1_1_regwrite));
  Comm2 comm2_1 (
    .Func(Func), .RegDst(comm2_1_regdst), .Jump(comm2_1_jump), .Branch(comm2_1_branch),
    .MemRead(comm2_1_memread), .MemtoReg(comm2_1_memtoreg), .MemWrite(comm2_1_memwrite),
    .ALUSrc(comm2_1_alusrc), .RegWrite(comm2_1_regwrite));
  AllZero allzero_1 (.Inp(Op), .AllZero(allzero_1_allzero));
  Multiplexer #(.enable("false")) multiplexer_1 (
    .in0(comm2_1_regdst), .in1(comm1_1_regdst), .out(RegDst), .sel(allzero_1_allzero));
  Multiplexer #(.enable("false")) multiplexer_2 (
    .in0(comm2_1_jump), .in1(comm1_1_jump), .out(Jump), .sel(allzero_1_allzero));
  Multiplexer #(.enable("false")) multiplexer_3 (
    .in0(comm2_1_branch), .in1(comm1_1_branch), .out(Branch), .sel(allzero_1_allzero));
  Multiplexer #(.enable("false")) multiplexer_4 (
    .in0(comm2_1_memread), .in1(comm1_1_memread), .out(MemRead), .sel(allzero_1_allzero));
  Multiplexer #(.enable("false")) multiplexer_5 (
    .in0(comm2_1_memtoreg), .in1(comm1_1_memtoreg), .out(MemtoReg), .sel(allzero_1_allzero));
  Multiplexer #(.enable("false")) multiplexer_6 (
    .in0(comm2_1_memwrite), .in1(comm1_1_memwrite), .out(MemWrite), .sel(allzero_1_allzero));
  Multiplexer #(.enable("false")) multiplexer_7 (
    .in0(comm2_1_alusrc), .in1(comm1_1_alusrc), .out(ALUSrc), .sel(allzero_1_allzero));
  Multiplexer #(.enable("false")) multiplexer_8 (
    .in0(comm2_1_regwrite), .in1(comm1_1_regwrite), .out(RegWrite), .sel(allzero_1_allzero));
endmodule

module Comm2 (
  input  [5:0] Func,
  output RegDst,
  output Jump,
  output Branch,
  output MemRead,
  output MemtoReg,
  output MemWrite,
  output ALUSrc,
  output RegWrite
);

  wire not_1_out, not_2_out, not_3_out;

  not not_1 (not_1_out, Func[3]);
  not not_2 (not_2_out, Func[1]);
  not not_3 (not_3_out, Func[3]);
  or or_1 (RegDst, not_1_out, Func[5]);
  and and_1 (Jump, Func[3], not_2_out);
  or or_2 (RegWrite, not_3_out, Func[1]);

  assign ALUSrc = 1'b0;
  assign Branch = 1'b0;
  assign MemRead = 1'b0;
  assign MemtoReg = 1'b0;
  assign MemWrite = 1'b0;
endmodule

module OpToAlu (
  input  Op1,
  input  Op2,
  input  Op3,
  input  Op4,
  input  Op5,
  input  Op6,
  output Alu1,
  output Alu2,
  output Alu3,
  output Alu4
);

  wire and_1_out, and_2_out, and_3_out, and_4_out, and_5_out, not_1_out, not_2_out, not_3_out, not_4_out,
       not_5_out, not_6_out, not_7_out, not_8_out, not_9_out, not_10_out, not_11_out;

  not not_1 (not_1_out, Op1);
  not not_2 (not_2_out, Op6);
  not not_3 (not_3_out, Op1);
  not not_4 (not_4_out, Op4);
  not not_5 (not_5_out, Op5);
  not not_6 (not_6_out, Op1);
  not not_7 (not_7_out, Op4);
  not not_8 (not_8_out, Op6);
  not not_9 (not_9_out, Op5);
  not not_10 (not_10_out, Op3);
  not not_11 (not_11_out, Op4);
  and and_1 (and_1_out, not_1_out, not_2_out);
  and and_2 (and_2_out, not_3_out, not_4_out, Op5);
  and and_3 (and_3_out, Op3, Op4, not_5_out);
  and and_4 (and_4_out, not_6_out, not_7_out, Op5);
  and and_5 (and_5_out, Op5, not_8_out);
  or or_1 (Alu3, not_9_out, Op1);
  or or_2 (Alu4, not_10_out, not_11_out);
  or or_3 (Alu1, and_1_out, and_2_out, and_3_out);
  or or_4 (Alu2, and_4_out, and_5_out);
endmodule

module FuncToAlu (
  input  F1,
  input  F2,
  input  F3,
  input  F4,
  input  F5,
  input  F6,
  output Alu1,
  output Alu2,
  output Alu3,
  output Alu4
);

  wire and_1_out, and_3_out, not_1_out, not_2_out;

  and and_1 (and_1_out, F1, F4);
  and and_2 (Alu3, F1, F6);
  not not_1 (not_1_out, F1);
  or or_1 (Alu1, F3, and_1_out);
  not not_2 (not_2_out, F4);
  and and_3 (and_3_out, not_1_out, F6);
  or or_2 (Alu4, not_2_out, and_3_out);

  assign Alu2 = F5;
endmodule
